# Fritzing sketch Arduino Clock (saved by Fritzing 0.9.10b)

parts:
  Componente1 = Arduino Uno (Rev3)
  LCD_DISPLAY_SCREEN_16x2 = LCD Display 16x2
  Convertitore_Expander_seriale = LCM1602 IIC [chip_label="Modulo " part_number="LCM1602 IIC" package="DIP (Dual Inline) [THT]"]
  DS1302_RTC_MODULE = RTC_DS1302_module

nets:
  N1: Componente1.A4/SDA, Convertitore_Expander_seriale.SDA
  N2: Componente1.A5/SCL, Convertitore_Expander_seriale.SCL
  N3: Componente1.D2, DS1302_RTC_MODULE.RST
  N4: Componente1.D3_PWM, DS1302_RTC_MODULE.DAT
  N5: Componente1.D4, DS1302_RTC_MODULE.CLK
  N6: LCD_DISPLAY_SCREEN_16x2.aún_sin_nombre#0, Convertitore_Expander_seriale.VSS
  N7: LCD_DISPLAY_SCREEN_16x2.aún_sin_nombre#1, Convertitore_Expander_seriale.VDD
  N8: LCD_DISPLAY_SCREEN_16x2.aún_sin_nombre#2, Convertitore_Expander_seriale.V0
  N9: LCD_DISPLAY_SCREEN_16x2.aún_sin_nombre#3, Convertitore_Expander_seriale.RS
  N10: LCD_DISPLAY_SCREEN_16x2.aún_sin_nombre#4, Convertitore_Expander_seriale.RW
  N11: LCD_DISPLAY_SCREEN_16x2.aún_sin_nombre#5, Convertitore_Expander_seriale.E
  N12: LCD_DISPLAY_SCREEN_16x2.aún_sin_nombre#6, Convertitore_Expander_seriale.D0
  N13: LCD_DISPLAY_SCREEN_16x2.aún_sin_nombre#7, Convertitore_Expander_seriale.D1
  N14: LCD_DISPLAY_SCREEN_16x2.aún_sin_nombre#8, Convertitore_Expander_seriale.D2
  N15: LCD_DISPLAY_SCREEN_16x2.aún_sin_nombre#9, Convertitore_Expander_seriale.D3
  N16: LCD_DISPLAY_SCREEN_16x2.aún_sin_nombre#10, Convertitore_Expander_seriale.D4
  N17: LCD_DISPLAY_SCREEN_16x2.aún_sin_nombre#11, Convertitore_Expander_seriale.D5
  N18: LCD_DISPLAY_SCREEN_16x2.aún_sin_nombre#12, Convertitore_Expander_seriale.D6
  N19: LCD_DISPLAY_SCREEN_16x2.aún_sin_nombre#13, Convertitore_Expander_seriale.D7
  N20: LCD_DISPLAY_SCREEN_16x2.aún_sin_nombre#14, Convertitore_Expander_seriale.A
  N21: LCD_DISPLAY_SCREEN_16x2.aún_sin_nombre#15, Convertitore_Expander_seriale.K
  GND: Convertitore_Expander_seriale.GND, DS1302_RTC_MODULE.GND
  VCC: Convertitore_Expander_seriale.VCC, DS1302_RTC_MODULE.VCC
  N22: Convertitore_Expander_seriale.LED_A, Convertitore_Expander_seriale.LED_B

custom parts:
  LCM1602 IIC: I2C-Module to use a 1602 or 2004 LCD on with the wire.h libory Serial LCD Modul
  RTC_DS1302_module: Arduino module DS1302 SPI Real Time Clock

// code stored in the sketch: Untitled2.ino
/*

*/

#include <DS1302.h>
#include <Wire.h>
#include <LiquidCrystal_I2C.h>
DS1302 rtc(2, 3, 4);
LiquidCrystal_I2C lcd(0x27, 16, 2); 

void setup()
{
  rtc.halt(false);
  rtc.writeProtect(false);  
  Serial.begin(9600); 
  lcd.init();
  lcd.backlight();

}

void loop()
{
  Serial.print(rtc.getDOWStr());
  Serial.print(" ");
  Serial.print(rtc.getDateStr());
  Serial.print(" -- ");
  Serial.println(rtc.getTimeStr());
  lcd.clear();
  data (); 
  ora (); 
  delay (1000);
}

void data ()
{
  lcd.setCursor(0, 0);
  lcd.print(rtc.getDOWStr());
  lcd.print(" ");
  lcd.print(rtc.getDateStr());
}

void ora()
{
  lcd.setCursor(0, 1);
  lcd.print(rtc.getTimeStr());
}
